# Fritzing sketch ethernet and dht111 (saved by Fritzing 0.9.2b)
breadboards: 1

parts:
  Part1 = Arduino Ethernet Shield (Rev3)
  DHT1 = DHT11 Humitidy and Temperature Sensor
  R1 = Resistor [tolerance=±5% resistance=4.7k package=THT]

nets:
  N1: Part1.D2, DHT1.DATA
  5V: Part1.5V, DHT1.VDD, R1.Pin_0, R1.Pin_1
  GND: Part1.GND, DHT1.GND

custom parts:
  DHT11 Humitidy and Temperature Sensor: DHT11 Humidity and Temperature Sensor
