# Fritzing sketch ethernet led (saved by Fritzing 0.9.2b)

parts:
  Part1 = Arduino Ethernet Shield (Rev3)
  LED1 = LED - 5mm [color="Red (633nm)" package="5 mm [THT]"]
  R1 = Resistor [tolerance=±5% resistance=470 package=THT]

nets:
  N1: Part1.GND, LED1.cathode
  N2: Part1.D7, R1.Pin_1
  N3: LED1.anode, R1.Pin_0
