# Fritzing sketch ethernet regb led (saved by Fritzing 0.9.2b)

parts:
  Part1 = Arduino Ethernet Shield (Rev3)
  LED1 = RGB LED (com. cathode, rgb) [package="5 mm [THT]"]
  R1 = Resistor [tolerance=±5% resistance=220 package=THT]
  R2 = Resistor [tolerance=±5% resistance=220 package=THT]
  R3 = Resistor [tolerance=±5% resistance=220 package=THT]

nets:
  N1: Part1.D8, R2.Pin_0
  N2: Part1.GND, LED1.common_cathode
  N3: Part1.PWM_D6, R3.Pin_0
  N4: Part1.D7, R1.Pin_0
  N5: LED1.red_anode, R1.Pin_1
  N6: LED1.green_anode, R3.Pin_1
  N7: LED1.blue_anode, R2.Pin_1
