# Fritzing sketch ethernet switch example (saved by Fritzing 0.9.2b)

parts:
  Part1 = Arduino Ethernet Shield (Rev3)
  S1 = Pushbutton [package=THT]
  R1 = Resistor [tolerance=±5% resistance=1k package=THT]

nets:
  N1: Part1.GND, S1.leg0
  N2: Part1.D7, S1.leg1, R1.Pin_1
  N3: Part1.5V, R1.Pin_0
