# Fritzing sketch ‌linkitone and L3GD20 (saved by Fritzing 0.9.3b)

parts:
  Part1 = LinkIt ONE
  Part2 = L3GD20H Triple-Axis Gyro Breakout Board [part_number=1032]

nets:
  N1: Part1.SDA, Part2.SDA/SDI/SDO
  N2: Part1.SCL, Part2.SCL/SPC
  3.3V: Part1.3.3V, Part2.+3V3
  GND: Part1.GND, Part2.GND

custom parts:
  LinkIt ONE: All-in-one development board with GSM/GPRS, Bluetooth 2.0/4.0, Wi-Fi, GPS. Compatible to Arduino IDE.
  L3GD20H Triple-Axis Gyro Breakout Board: This breakout board is based around the latest gyro technology, the L3GD20H from STMicro. It's the upgrade to the L3G4200 with three full axes of sensing. The chip can be set to ±250, ±500, or ±2000 degree-per-second scale for a large range of sensitivity. The chip supports both I2C and SPI so you can interface with any microcontroller easily. Includes level shifting circuitry so you can use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
