# Fritzing sketch ‌linkitone and adxl345 (saved by Fritzing 0.9.3b)

parts:
  Part1 = LinkIt ONE
  Part3 = Adafruit ADXL345 [part_number="Adafruit #1231"]

nets:
  N1: Part1.SDA, Part3.SDA/SDIO
  N2: Part1.SCL, Part3.SCL
  3.3V: Part1.3.3V, Part3.3.3V
  GND: Part1.GND, Part3.GND

custom parts:
  LinkIt ONE: All-in-one development board with GSM/GPRS, Bluetooth 2.0/4.0, Wi-Fi, GPS. Compatible to Arduino IDE.
  Adafruit ADXL345: Filling out our accelerometer offerings, we now have the really lovely digital ADXL345 from Analog Devices, a triple-axis accelerometer with digital I2C and SPI interface breakout. We added an on-board 3.3V regulator and logic-level shifting circuitry, making it a perfect choice for interfacing with any 3V or 5V microcontroller such as the Arduino. The sensor has three axes of measurements, X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
