# Fritzing sketch ‌linkitone and bmp180 (saved by Fritzing 0.9.3b)

parts:
  Part1 = LinkIt ONE
  Part3 = Adafruit BMP180

nets:
  N1: Part1.SDA, Part3.SDA
  N2: Part1.SCL, Part3.SCL
  3.3V: Part1.3.3V, Part3.+3V3
  GND: Part1.GND, Part3.GND

custom parts:
  LinkIt ONE: All-in-one development board with GSM/GPRS, Bluetooth 2.0/4.0, Wi-Fi, GPS. Compatible to Arduino IDE.
  Adafruit BMP180: This precision sensor from Bosch is the best low-cost sensing solution for measuring barometric pressure and temperature. Because pressure changes with altitude you can also use it as an altimeter! The sensor is soldered onto a PCB with a 3.3V regulator, I2C level shifter and pull-up resistors on the I2C pins. The BMP180 is the next-generation of sensors from Bosch, and replaces the BMP085.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
