# Fritzing sketch ‌linkitone and hdc1008 (saved by Fritzing 0.9.3b)

parts:
  Part1 = LinkIt ONE
  Part2 = Adafruit HDC1008 Temperature Humidity Sensor [part_number="Adafruit #2635"]

nets:
  N1: Part1.SDA, Part2.SDA
  N2: Part1.SCL, Part2.SCL
  3.3V: Part1.3.3V, Part2.VDD
  GND: Part1.GND, Part2.GND

custom parts:
  LinkIt ONE: All-in-one development board with GSM/GPRS, Bluetooth 2.0/4.0, Wi-Fi, GPS. Compatible to Arduino IDE.
  Adafruit HDC1008 Temperature Humidity Sensor: This I2C digital humidity sensor is a fairly accurate and intelligent alternative to the much simpler Humidity and Temperature Sensor - SHT15 Breakout It has a typical accuracy of ±4% with an operating range that's optimized from 10% to 80% RH. Operation outside this range is still possible - just the accuracy might drop a bit. The temperature output has a typical accuracy of ±0.2°C from -20~85°C.
