# Fritzing sketch ‌linkitone and hmc5883 (saved by Fritzing 0.9.3b)

parts:
  Part1 = LinkIt ONE
  Part2 = Triple Axis Magnetometer - HMC5883 Breakout

nets:
  N1: Part1.SDA, Part2.SDA
  N2: Part1.SCL, Part2.SCL
  3.3V: Part1.3.3V, Part2.VCC
  GND: Part1.GND, Part2.GND

custom parts:
  LinkIt ONE: All-in-one development board with GSM/GPRS, Bluetooth 2.0/4.0, Wi-Fi, GPS. Compatible to Arduino IDE.
