# Fritzing sketch ‌linkitone and lm35 (saved by Fritzing 0.9.3b)

parts:
  Part1 = LinkIt ONE
  T1 = LM35 Temperature Sensor [package="TO92 [THT]"]

nets:
  N1: Part1.A0, T1.Vout
  N2: Part1.5V, T1.+Vs
  GND: Part1.GND, T1.GND

custom parts:
  LinkIt ONE: All-in-one development board with GSM/GPRS, Bluetooth 2.0/4.0, Wi-Fi, GPS. Compatible to Arduino IDE.
