# Fritzing sketch ‌linkitone and mag3110 (saved by Fritzing 0.9.3b)

parts:
  Part1 = LinkIt ONE
  U1 = MAG3110 [package=dfn-10]

nets:
  N1: Part1.SDA, U1.SDA
  N2: Part1.SCL, U1.SCL
  N3: Part1.3.3V, U1.VDDIO
  GND: Part1.GND, U1.GND

custom parts:
  LinkIt ONE: All-in-one development board with GSM/GPRS, Bluetooth 2.0/4.0, Wi-Fi, GPS. Compatible to Arduino IDE.
