# Fritzing sketch ‌linkitone and mcp9808 (saved by Fritzing 0.9.3b)

parts:
  Part1 = LinkIt ONE
  Part4 = MCP9808 High Accuracy I2C Temperature Sensor [part_number=1782]

nets:
  N1: Part1.SDA, Part4.SDA
  N2: Part1.SCL, Part4.SCL
  3.3V: Part1.3.3V, Part4.VDD
  GND: Part1.GND, Part4.GND

custom parts:
  LinkIt ONE: All-in-one development board with GSM/GPRS, Bluetooth 2.0/4.0, Wi-Fi, GPS. Compatible to Arduino IDE.
  MCP9808 High Accuracy I2C Temperature Sensor: This I2C digital temperature sensor is one of the more accurate/precise we've ever seen, with a typical accuracy of ±0.25°C over the sensor's -40°C to +125°C range and precision of +0.0625°C. They work great with any microcontroller using standard i2c. There are 3 address pins so you can connect up to 8 to a single I2C bus without address collisions. Best of all, a wide voltage range makes is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
