# Fritzing sketch ‌linkitone and mlx90614 (saved by Fritzing 0.9.3b)

parts:
  Part1 = LinkIt ONE
  U1 = MLX90614 [package=to-39]

nets:
  N1: Part1.SDA, U1.PWM_SDA
  N2: Part1.SCL, U1.SCL_VZ
  3.3V: Part1.3.3V, U1.VDD
  GND: Part1.GND, U1.VSS

custom parts:
  LinkIt ONE: All-in-one development board with GSM/GPRS, Bluetooth 2.0/4.0, Wi-Fi, GPS. Compatible to Arduino IDE.
