# Fritzing sketch ‌linkitone and mma8451 (saved by Fritzing 0.9.3b)

parts:
  Part1 = LinkIt ONE
  Part2 = Adafruit MMA8451 Accelerometer [part_number="Adafruit #2019"]

nets:
  N1: Part1.SDA, Part2.SDA
  N2: Part1.SCL, Part2.SCL
  3.3V: Part1.3.3V, Part2.+3V3
  GND: Part1.GND, Part2.GND

custom parts:
  LinkIt ONE: All-in-one development board with GSM/GPRS, Bluetooth 2.0/4.0, Wi-Fi, GPS. Compatible to Arduino IDE.
  Adafruit MMA8451 Accelerometer: So many accelerometers and so little time! We've expanded our accelerometer selection even more with this high-precision and inexpensive MMA8451 Triple-Axis Accelerometer w/ 14-bit ADC. You can detect motion, tilt and basic orientation with a digital accelerometer - and the MMA8451 is a great accelerometer to start with. It has a wide usage range, from +-2g up to +-8g yet is easy to use with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
