# Fritzing sketch ‌linkitone and sht31 (saved by Fritzing 0.9.3b)

parts:
  Part1 = LinkIt ONE
  Part2 = Adafruit SHT31-D Sensirion Temperature/Humidity Sensor [part_number="Adafruit #2857"]

nets:
  N1: Part1.SDA, Part2.SDA
  N2: Part1.SCL, Part2.SCL
  3.3V: Part1.3.3V, Part2.VIN
  GND: Part1.GND, Part2.GND

custom parts:
  LinkIt ONE: All-in-one development board with GSM/GPRS, Bluetooth 2.0/4.0, Wi-Fi, GPS. Compatible to Arduino IDE.
  Adafruit SHT31-D Sensirion Temperature/Humidity Sensor: Sensirion Temperature/Humidity sensors are some of the finest & highest-accuracy devices you can get. And, finally we have some that have a true I2C interface for easy reading. The SHT31-D sensor has an excellent ±2% relative humidity and ±0.3°C accuracy for most uses. Unlike earlier SHT sensors, this sensor has a true I2C interface, and (bonus!) even with two address options. It also is 3V or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
