# Fritzing sketch wemos rgbled (saved by Fritzing 0.9.2b)

parts:
  WeMos_D1_Mini1 = WeMos D1 Mini
  LED1 = RGB LED (com. cathode, rgb) [package="5 mm [THT]"]
  R1 = Resistor [tolerance=±5% resistance=1k package=THT]
  R2 = Resistor [tolerance=±5% resistance=1k package=THT]
  R3 = Resistor [tolerance=±5% resistance=1k package=THT]

nets:
  N1: WeMos_D1_Mini1.D5, R1.Pin_0
  N2: WeMos_D1_Mini1.D6, R2.Pin_0
  N3: WeMos_D1_Mini1.D7, R3.Pin_0
  N4: WeMos_D1_Mini1.G, LED1.common_cathode
  N5: LED1.red_anode, R1.Pin_1
  N6: LED1.green_anode, R3.Pin_1
  N7: LED1.blue_anode, R2.Pin_1
